// Logisim project alu.circ as structural Verilog: 2 circuits, main circuit main
module main (
  input  Vem_1,
  input  INV_A,
  input  A,
  input  EN_A,
  input  B,
  input  EN_B,
  input  F0,
  input  F1,
  output out_9,
  output Vai_1
);

  wire and_1_out, and_2_out, and_3_out, and_4_out, and_5_out, and_6_out, and_7_out, and_8_out, and_9_out,
       decoder_1_out0, decoder_1_out1, decoder_1_out2, decoder_1_out3, not_1_out, or_1_out, xor_1_out,
       xor_2_out, xor_3_out;

  and and_1 (and_1_out, A, EN_A);
  and and_2 (and_2_out, B, EN_B);
  Decoder #(.select(2)) decoder_1 (
    .out0(decoder_1_out0), .out1(decoder_1_out1), .out2(decoder_1_out2), .out3(decoder_1_out3), .sel({F0, F1}));  // open: en
  xor xor_1 (xor_1_out, INV_A, and_1_out);
  and and_3 (and_3_out, xor_1_out, and_2_out);
  or or_1 (or_1_out, xor_1_out, and_2_out);
  not not_1 (not_1_out, and_2_out);
  and and_4 (and_4_out, decoder_1_out3, xor_1_out, and_2_out);
  xor xor_2 (xor_2_out, and_2_out, xor_1_out);
  and and_5 (and_5_out, decoder_1_out3, xor_2_out, Vem_1);
  or or_2 (Vai_1, and_4_out, and_5_out);
  and and_6 (and_6_out, and_3_out, decoder_1_out0);
  and and_7 (and_7_out, or_1_out, decoder_1_out1);
  and and_8 (and_8_out, not_1_out, decoder_1_out2);
  xor xor_3 (xor_3_out, Vem_1, xor_2_out);
  and and_9 (and_9_out, xor_3_out, decoder_1_out3);
  or or_3 (out_9, and_6_out, and_7_out, and_8_out, and_9_out);
endmodule

module alu_8_bits (
  input  INVA,
  input  ENA,
  input  ENB,
  input  F0,
  input  F1,
  input  A0,
  input  B0,
  input  A1,
  input  B1,
  input  A3,
  input  B3,
  input  A4,
  input  B4,
  input  A5,
  input  B5,
  input  A6,
  input  B6,
  input  A7,
  input  B7,
  input  A2,
  input  B2
);

  wire main_2_vai_1, main_3_vai_1, main_4_vai_1, main_5_vai_1, main_6_vai_1, main_7_vai_1, main_8_vai_1;
  wire [8:0] main_8_out_9;

  main main_1 (
    .INV_A(INVA), .A(A0), .EN_A(ENA), .B(B0), .EN_B(ENB), .F0(F0), .F1(F1), .Vem_1(main_2_vai_1),
    .Vai_1(main_8_out_9[8]), .out_9(main_8_out_9[7]));
  main main_2 (
    .INV_A(INVA), .A(A1), .EN_A(ENA), .B(B1), .EN_B(ENB), .F0(F0), .F1(F1), .Vem_1(main_3_vai_1),
    .Vai_1(main_2_vai_1), .out_9(main_8_out_9[6]));
  main main_3 (
    .INV_A(INVA), .A(A2), .EN_A(ENA), .B(B2), .EN_B(ENB), .F0(F0), .F1(F1), .Vem_1(main_4_vai_1),
    .Vai_1(main_3_vai_1), .out_9(main_8_out_9[5]));
  main main_4 (
    .INV_A(INVA), .A(A3), .EN_A(ENA), .B(B3), .EN_B(ENB), .F0(F0), .F1(F1), .Vem_1(main_5_vai_1),
    .Vai_1(main_4_vai_1), .out_9(main_8_out_9[4]));
  main main_5 (
    .INV_A(INVA), .A(A4), .EN_A(ENA), .B(B4), .EN_B(ENB), .F0(F0), .F1(F1), .Vem_1(main_6_vai_1),
    .Vai_1(main_5_vai_1), .out_9(main_8_out_9[3]));
  main main_6 (
    .INV_A(INVA), .A(A5), .EN_A(ENA), .B(B5), .EN_B(ENB), .F0(F0), .F1(F1), .Vem_1(main_7_vai_1),
    .Vai_1(main_6_vai_1), .out_9(main_8_out_9[2]));
  main main_7 (
    .INV_A(INVA), .A(A6), .EN_A(ENA), .B(B6), .EN_B(ENB), .F0(F0), .F1(F1), .Vem_1(main_8_vai_1),
    .Vai_1(main_7_vai_1), .out_9(main_8_out_9[1]));
  main main_8 (
    .INV_A(INVA), .A(A7), .EN_A(ENA), .B(B7), .EN_B(ENB), .F0(F0), .F1(F1), .Vai_1(main_8_vai_1),
    .out_9(main_8_out_9[0]));  // open: Vem_1
endmodule
